// Logisim project alu.circ as structural Verilog: 2 circuits, main circuit ALU
module ALU (
  input  [7:0] A,
  input  [7:0] B,
  input  [2:0] S,
  output [7:0] Out,
  output ZF,
  output VF
);

  wire and_3_out, multiplexer_3_out, xnor_1_out, xor_1_out;
  wire [7:0] adder_1_out, and_1_out, multiplexer_1_out, multiplexer_2_out, not_1_out, not_2_out, or_1_out;

  Multiplexer #(.select(2), .width(8), .enable("false")) multiplexer_1 (
    .in0(A), .in1(B), .in2(A), .in3(A), .out(multiplexer_1_out), .sel({S[2], S[0]}));
  assign not_1_out = ~B;  // NOT_Gate not_1, 8 bits wide
  Multiplexer #(.select(2), .width(8), .enable("false")) multiplexer_2 (
    .in0(8'h1), .in1(8'h1), .in2(B), .in3(not_1_out), .out(multiplexer_2_out), .sel({S[2], S[0]}));
  Adder adder_1 (
    .a(multiplexer_1_out), .b(multiplexer_2_out), .out(adder_1_out), .cin(multiplexer_3_out));  // open: cout
  Multiplexer #(.select(3), .enable("false")) multiplexer_3 (
    .in0(1'b0), .in1(1'b0), .in2(1'b0), .in3(1'b0), .in4(1'b0), .in5(1'b1), .in6(1'b0), .in7(1'b0),
    .out(multiplexer_3_out), .sel(S));
  assign and_1_out = A & B;  // AND_Gate and_1, 8 bits wide
  assign or_1_out = A | B;  // OR_Gate or_1, 8 bits wide
  Multiplexer #(.select(3), .width(8), .enable("false")) multiplexer_4 (
    .in0(A), .in1(B), .in2(adder_1_out), .in3(adder_1_out), .in4(adder_1_out), .in5(adder_1_out),
    .in6(and_1_out), .in7(or_1_out), .out(Out), .sel(S));
  assign not_2_out = ~Out;  // NOT_Gate not_2, 8 bits wide
  xnor xnor_1 (xnor_1_out, multiplexer_1_out[7], multiplexer_2_out[7]);
  xor xor_1 (xor_1_out, Out[7], multiplexer_1_out[7]);
  and and_2 (ZF, not_2_out[7], not_2_out[6], not_2_out[5], not_2_out[4], not_2_out[3], not_2_out[2], not_2_out[1], not_2_out[0]);
  Multiplexer #(.select(3), .enable("false")) multiplexer_5 (
    .in0(1'b0), .in1(1'b0), .in2(and_3_out), .in3(and_3_out), .in4(and_3_out), .in5(and_3_out), .in6(1'b0),
    .in7(1'b0), .out(VF), .sel(S));
  and and_3 (and_3_out, xnor_1_out, xor_1_out);
endmodule

module test (
  input  [7:0] in_1,
  input  [7:0] in_2,
  input  [2:0] in_3,
  output [7:0] out_4,
  output out_5,
  output out_6
);

  ALU alu_1 (.A(in_1), .B(in_2), .Out(out_4), .ZF(out_5), .VF(out_6), .S(in_3));
endmodule
