// Logisim project CPU.circ as structural Verilog: 3 circuits, main circuit datapath
module datapath (
  input  [7:0] Input,
  input  RST,
  output halt,
  output [7:0] Out
);

  wire A_Enable, B_Enable, CLK, MBR_Enable, OUT_Enable, PC_Enable;
  wire [1:0] B_Select;
  wire [2:0] S;
  wire [7:0] A_q, alu_1_out, B_q, Data, MBR_q, multiplexer_1_out, PC_q;

  // Probe on alu_1_out
  Register A (.D(alu_1_out), .en(A_Enable), .Q(A_q), .clk(CLK), .clr(RST));
  Register B (.D(alu_1_out), .en(B_Enable), .Q(B_q), .clk(CLK), .clr(RST));
  Register MBR (.D(Data), .en(MBR_Enable), .Q(MBR_q), .clk(CLK), .clr(RST));
  Register PC (.D(alu_1_out), .en(PC_Enable), .Q(PC_q), .clk(CLK), .clr(RST));
  Register u_OUT (.D(alu_1_out), .en(OUT_Enable), .Q(Out), .clk(CLK), .clr(RST));
  Clock u_CLK (.out(CLK));
  Hex_Digit_Display hex_digit_display_1 (.value(Out[7:4]));  // open: dp
  Hex_Digit_Display hex_digit_display_2 (.value(Out[3:0]));  // open: dp
  Multiplexer #(.select(2), .width(8), .enable("false")) multiplexer_1 (
    .in0(B_q), .in1(MBR_q), .in2(PC_q), .in3(Input), .out(multiplexer_1_out), .sel(B_Select));
  ALU alu_1 (.A(A_q), .Out(alu_1_out), .B(multiplexer_1_out), .S(S));  // open: ZF, VF
  control control_1 (
    .From_MBR(MBR_q[4:0]), .RST(RST), .Halt(halt),
    .Write_Enables({A_Enable, B_Enable, MBR_Enable, PC_Enable, OUT_Enable}), .B_Select(B_Select),
    .ALU_Select(S), .CLK(CLK));
  RAM #(.bus("asynch")) ram_1 (.addr(PC_q), .data(Data));  // open: sel, ld, clr

  // Notes on the sheet:
  //   Program Store
endmodule

module ALU (
  input  [7:0] A,
  input  [7:0] B,
  input  [2:0] S,
  output [7:0] Out,
  output ZF,
  output VF
);

  wire and_3_out, multiplexer_3_out, xnor_1_out, xor_1_out;
  wire [7:0] adder_1_out, and_1_out, multiplexer_1_out, multiplexer_2_out, not_1_out, not_2_out, or_1_out;

  Multiplexer #(.select(2), .width(8), .enable("false")) multiplexer_1 (
    .in0(A), .in1(B), .in2(A), .in3(A), .out(multiplexer_1_out), .sel({S[2], S[0]}));
  assign not_1_out = ~B;  // NOT_Gate not_1, 8 bits wide
  Multiplexer #(.select(2), .width(8), .enable("false")) multiplexer_2 (
    .in0(8'h1), .in1(8'h1), .in2(B), .in3(not_1_out), .out(multiplexer_2_out), .sel({S[2], S[0]}));
  Adder adder_1 (
    .a(multiplexer_1_out), .b(multiplexer_2_out), .out(adder_1_out), .cin(multiplexer_3_out));  // open: cout
  Multiplexer #(.select(3), .enable("false")) multiplexer_3 (
    .in0(1'b0), .in1(1'b0), .in2(1'b0), .in3(1'b0), .in4(1'b0), .in5(1'b1), .in6(1'b0), .in7(1'b0),
    .out(multiplexer_3_out), .sel(S));
  assign and_1_out = A & B;  // AND_Gate and_1, 8 bits wide
  assign or_1_out = A | B;  // OR_Gate or_1, 8 bits wide
  Multiplexer #(.select(3), .width(8), .enable("false")) multiplexer_4 (
    .in0(A), .in1(B), .in2(adder_1_out), .in3(adder_1_out), .in4(adder_1_out), .in5(adder_1_out),
    .in6(and_1_out), .in7(or_1_out), .out(Out), .sel(S));
  assign not_2_out = ~Out;  // NOT_Gate not_2, 8 bits wide
  xnor xnor_1 (xnor_1_out, multiplexer_1_out[7], multiplexer_2_out[7]);
  xor xor_1 (xor_1_out, Out[7], multiplexer_1_out[7]);
  and and_2 (ZF, not_2_out[7], not_2_out[6], not_2_out[5], not_2_out[4], not_2_out[3], not_2_out[2], not_2_out[1], not_2_out[0]);
  and and_3 (and_3_out, xnor_1_out, xor_1_out);
  Multiplexer #(.select(3), .enable("false")) multiplexer_5 (
    .in0(1'b0), .in1(1'b0), .in2(and_3_out), .in3(and_3_out), .in4(and_3_out), .in5(and_3_out), .in6(1'b0),
    .in7(1'b0), .out(VF), .sel(S));
endmodule

module control (
  input  [4:0] From_MBR,
  input  RST,
  input  CLK,
  output Halt,
  output [4:0] Write_Enables,
  output [1:0] B_Select,
  output [2:0] ALU_Select
);

  wire not_1_out;
  wire [4:0] IR_q_2, multiplexer_1_out, SPC_q;
  wire [10:10] IR_q;
  wire [15:0] rom_1_data;

  Multiplexer #(.width(5), .enable("false")) multiplexer_1 (
    .in0(IR_q_2), .in1(From_MBR), .out(multiplexer_1_out), .sel(IR_q[10]));
  Register #(.width(5)) SPC (.D(multiplexer_1_out), .Q(SPC_q), .clk(CLK), .clr(RST));  // open: en
  ROM #(.addrWidth(5), .dataWidth(16)) rom_1 (.addr(SPC_q), .data(rom_1_data));  // open: sel
  Register #(.width(16), .trigger("falling")) IR (
    .D(rom_1_data), .Q({IR_q_2, IR_q[10], ALU_Select, B_Select, Write_Enables}), .clk(CLK), .clr(RST));  // open: en
  and and_1 (Halt, SPC_q[4], SPC_q[3], SPC_q[2], not_1_out, SPC_q[0]);
  not not_1 (not_1_out, SPC_q[1]);

  // Notes on the sheet:
  //   contents of rom_1 (hex, n*v repeats v):
  //   804 11c0 19c2 400 28e0 30f0 0 4000 4801 0 5804 60a0 68a2 0 7804 80a0 88b0 91c0 99c2 0 a900 b110 0
  //   c000 c808 0 da00 e210 0 e800
endmodule
